# Fritzing sketch PYBOARD_ATECCX08A (saved by Fritzing 0.9.3b)
circuit board: 8.46667cm x 5.64444cm

parts:
  pyboard1 = Micro Python pyboard [part_number=PYBv10b]
  IC1 = IC, DIP package, 8 pins [chip_label=ATECC]

nets:
  N1: pyboard1.X9, IC1.pin6
  N2: pyboard1.X10, IC1.pin5
  N3: pyboard1.X14_GND, IC1.pin4
  N4: pyboard1.X15_3V3, IC1.pin8
